# Fritzing sketch esp32_ky40 (saved by Fritzing 1.0.4)

parts:
  esp1 = ESP32 DevKitc V4
  RE1 = KY-040 Rotary encoder [package=THT]
  RE2 = KY-040 Rotary encoder [package=THT]
  U1 = LuaNode32 / ESP32 [part_number=ESP32S-PIN30]  # not connected

nets:
  N1: esp1.IO16, RE1.CLK
  N2: esp1.IO17, RE1.DT
  N3: esp1.IO22, RE1.SW
  N4: esp1.IO23, RE2.SW
  N5: esp1.GND#18, RE1.GND
  N6: esp1.IO25, RE2.CLK
  N7: esp1.IO26, RE2.DT
  N8: esp1.GND#32, RE2.GND
  VCC: RE1.Vcc, RE2.Vcc

custom parts:
  ESP32 DevKitc V4: ESP32-DevKitC board with ESP32-WROOM-32 module. ESP32-DevKitC V4 is a small-sized ESP32-based development board produced by Espressif. Most of the pins on the ESP module are broken out to the pin headers on the board. The pins D0, D1, D2, D3, CMD and CLK are used internally for communication between ESP32 and SPI flash memory. They are grouped on both sides near the USB connector. Avoid using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
  KY-040 Rotary encoder: KY-040 Rotary Encoder with switch on breakout borad from AZ Delivery
  LuaNode32 / ESP32: New Image for LuaNode32 DOIT ESP32 DEVKIT V1. Base parts from LuaNode32 / ESP32 ESP32 based LuaNode32 by G.Noorlander DOIT Esp32 DevKit v1 (30 pins long, 11 pins width) by Werner Rothschopf (modified by vanepp Dec 2018)
